# Fritzing sketch ears-adxl (saved by Fritzing 0.7.10b)
stripboards: 1

parts:
  J1 = double row male pin header, 2 pins [form="♂ (male)"]
  J7 = male pin header, 3 pins [form="♂ (male)"]
  J8 = male pin header, 3 pins [form="♂ (male)"]
  J9 = male pin header, 3 pins [form="♂ (male)"]
  J10 = male pin header, 3 pins [form="♂ (male)"]
  R2 = Resistor [tolerance=±5% resistance=1k package="1206 [SMD]"]
  R1 = Resistor [tolerance=±5% resistance=1k package="1206 [SMD]"]
  J4 = rounded female pin header, 4 pins [form="♀ (female rounded)"]
  J6 = female pin header, 4 pins [form="♀ (female)"]
  U1 = mystery part, 3 pins [chip_label=3.3reg]
  J5 = female pin header, 4 pins [form="♀ (female)"]
  J3 = rounded female pin header, 1 pin [form="♀ (female rounded)"]

nets:
  N1: J1.pin1, J7.pin2, J8.pin2, J9.pin2, J10.pin2, U1.pin3
  N2: J1.pin2, J7.pin1, J8.pin1, J9.pin1, J10.pin1, J4.pin3, J6.pin1, U1.pin1
  N3: J7.pin3, J5.pin3
  N4: J8.pin3, J5.pin2
  N5: J9.pin3, J6.pin2
  N6: J10.pin3, J5.pin1
  N7: R2.Pin_0, J4.pin1, J6.pin3
  N8: R2.Pin_1, R1.Pin_1, J4.pin4, U1.pin2, J5.pin4, J3.pin1
  N9: R1.Pin_0, J4.pin2, J6.pin4
